// Logisim project 24-bit-mips.circ as structural Verilog: 5 circuits, main circuit main
module main (
  input  Reset,
  output [23:0] PC_Address
);

  wire alu_1_zero_flag, and_1_out, and_2_out, CLK_out, control_unit_1_aluop0, control_unit_1_aluop1,
       control_unit_1_alusrc, control_unit_1_beq, control_unit_1_bne, control_unit_1_jump,
       control_unit_1_memread, control_unit_1_memtoreg, control_unit_1_memwrite, control_unit_1_regdest,
       control_unit_1_regwrite, or_1_out;
  wire [2:0] alu_control_1_out_4;
  wire [3:0] adder_1_out_2, multiplexer_3_out;
  wire [3:3] alu_control_1_out_4_2;
  wire [19:0] adder_1_out;
  wire [23:0] adder_2_out, alu_1_output, bit_extender_1_out, multiplexer_1_out, multiplexer_2_out,
       multiplexer_4_out, multiplexer_5_out, ram_1_data, register_1_data01, register_1_data02, rom_1_data;

  Clock CLK (.out(CLK_out));
  Register_part #(.width(24)) PC (.D(multiplexer_2_out), .Q(PC_Address), .clk(CLK_out), .clr(Reset));  // open: en
  Adder #(.width(24)) adder_1 (.a(PC_Address), .b(24'h1), .out({adder_1_out_2, adder_1_out}));  // open: cin, cout
  ALU_control alu_control_1 (
    .ALUOp0(control_unit_1_aluop0), .ALUOp1(control_unit_1_aluop1),
    .out_4({alu_control_1_out_4_2[3], alu_control_1_out_4}), .Function(rom_1_data[3:0]));
  ROM #(.addrWidth(24), .dataWidth(24)) rom_1 (.addr(PC_Address), .data(rom_1_data));  // open: sel
  Control_Unit control_unit_1 (
    .Input(rom_1_data[23:20]), .RegDest(control_unit_1_regdest), .ALUSrc(control_unit_1_alusrc),
    .MemtoReg(control_unit_1_memtoreg), .RegWrite(control_unit_1_regwrite), .MemRead(control_unit_1_memread),
    .MemWrite(control_unit_1_memwrite), .BEQ(control_unit_1_beq), .BNE(control_unit_1_bne),
    .Jump(control_unit_1_jump), .ALUOp1(control_unit_1_aluop1), .ALUOp0(control_unit_1_aluop0));
  Adder #(.width(24)) adder_2 (
    .a({adder_1_out_2, adder_1_out}), .b(bit_extender_1_out), .out(adder_2_out));  // open: cin, cout
  assign bit_extender_1_out = {{12{1'b0}}, rom_1_data[11:0]};  // Bit_Extender bit_extender_1
  Multiplexer #(.width(24), .enable("false")) multiplexer_1 (
    .in0({adder_1_out_2, adder_1_out}), .in1(adder_2_out), .out(multiplexer_1_out), .sel(or_1_out));
  Multiplexer #(.width(24), .enable("false")) multiplexer_2 (
    .in0(multiplexer_1_out), .in1({adder_1_out_2, rom_1_data[19:0]}), .out(multiplexer_2_out),
    .sel(control_unit_1_jump));
  or or_1 (or_1_out, and_1_out, and_2_out);
  Multiplexer #(.width(4), .enable("false")) multiplexer_3 (
    .in0(rom_1_data[15:12]), .in1(rom_1_data[11:8]), .out(multiplexer_3_out), .sel(control_unit_1_regdest));
  and and_1 (and_1_out, control_unit_1_beq, alu_1_zero_flag);
  and and_2 (and_2_out, control_unit_1_bne, ~alu_1_zero_flag);  // AND_Gate
  Register register_1 (
    .Data01(register_1_data01), .Data02(register_1_data02), .Data_Address(multiplexer_3_out),
    .RS(rom_1_data[19:16]), .RT(rom_1_data[15:12]), .Clock(CLK_out),
    .Register_Write(control_unit_1_regwrite), .DATA_IN(multiplexer_5_out));
  Multiplexer #(.width(24), .enable("false")) multiplexer_4 (
    .in0(register_1_data02), .in1(bit_extender_1_out), .out(multiplexer_4_out), .sel(control_unit_1_alusrc));
  ALU alu_1 (
    .Shift(rom_1_data[7:4]), .Output(alu_1_output), .Zero_Flag(alu_1_zero_flag), .A(register_1_data01),
    .B(multiplexer_4_out), .Carry_IN(alu_control_1_out_4_2[3]), .Bit_inverter(alu_control_1_out_4_2[3]),
    .Operation(alu_control_1_out_4));  // open: Carry_OUT
  RAM #(.addrWidth(24), .dataWidth(24), .bus("separate")) ram_1 (
    .addr(alu_1_output), .din(register_1_data02), .data(ram_1_data), .str(control_unit_1_memwrite),
    .clk(CLK_out), .ld(control_unit_1_memread), .clr(Reset));  // open: sel
  Multiplexer #(.width(24), .enable("false")) multiplexer_5 (
    .in0(alu_1_output), .in1(ram_1_data), .out(multiplexer_5_out), .sel(control_unit_1_memtoreg));

  // Notes on the sheet:
  //   contents of rom_1 (hex, n*v repeats v):
  //   b00000 b11000 b22005 920003 b11001 b00001 f00003 12304 12305
endmodule

module Register (
  input  [23:0] DATA_IN,
  input  [3:0] RS,
  input  Clock,
  input  Register_Write,
  input  [3:0] Data_Address,
  input  [3:0] RT,
  output [23:0] Data01,
  output [23:0] Data02
);

  wire demultiplexer_1_out0, demultiplexer_1_out1, demultiplexer_1_out2, demultiplexer_1_out3,
       demultiplexer_1_out4, demultiplexer_1_out5, demultiplexer_1_out6, demultiplexer_1_out7,
       demultiplexer_1_out8, demultiplexer_1_out9, demultiplexer_1_out10, demultiplexer_1_out11,
       demultiplexer_1_out12, demultiplexer_1_out13, demultiplexer_1_out14, demultiplexer_1_out15;
  wire [23:0] register_1_q, register_2_q, register_3_q, register_4_q, register_5_q, register_6_q,
       register_7_q, register_8_q, register_9_q, register_10_q, register_11_q, register_12_q, register_13_q,
       register_14_q, register_15_q, register_16_q;

  Demultiplexer #(.select(4), .enable("false")) demultiplexer_1 (
    .out0(demultiplexer_1_out0), .out1(demultiplexer_1_out1), .out2(demultiplexer_1_out2),
    .out3(demultiplexer_1_out3), .out4(demultiplexer_1_out4), .out5(demultiplexer_1_out5),
    .out6(demultiplexer_1_out6), .out7(demultiplexer_1_out7), .out8(demultiplexer_1_out8),
    .out9(demultiplexer_1_out9), .out10(demultiplexer_1_out10), .out11(demultiplexer_1_out11),
    .out12(demultiplexer_1_out12), .out13(demultiplexer_1_out13), .out14(demultiplexer_1_out14),
    .out15(demultiplexer_1_out15), .in(Register_Write), .sel(Data_Address));
  Register_part #(.width(24)) register_1 (
    .D(DATA_IN), .en(demultiplexer_1_out0), .Q(register_1_q), .clk(Clock));  // open: clr
  Register_part #(.width(24)) register_2 (
    .D(DATA_IN), .en(demultiplexer_1_out1), .Q(register_2_q), .clk(Clock));  // open: clr
  Register_part #(.width(24)) register_3 (
    .D(DATA_IN), .en(demultiplexer_1_out2), .Q(register_3_q), .clk(Clock));  // open: clr
  Register_part #(.width(24)) register_4 (
    .D(DATA_IN), .en(demultiplexer_1_out3), .Q(register_4_q), .clk(Clock));  // open: clr
  Register_part #(.width(24)) register_5 (
    .D(DATA_IN), .en(demultiplexer_1_out4), .Q(register_5_q), .clk(Clock));  // open: clr
  Register_part #(.width(24)) register_6 (
    .D(DATA_IN), .en(demultiplexer_1_out5), .Q(register_6_q), .clk(Clock));  // open: clr
  Register_part #(.width(24)) register_7 (
    .D(DATA_IN), .en(demultiplexer_1_out6), .Q(register_7_q), .clk(Clock));  // open: clr
  Register_part #(.width(24)) register_8 (
    .D(DATA_IN), .en(demultiplexer_1_out7), .Q(register_8_q), .clk(Clock));  // open: clr
  Register_part #(.width(24)) register_9 (
    .D(DATA_IN), .en(demultiplexer_1_out8), .Q(register_9_q), .clk(Clock));  // open: clr
  Register_part #(.width(24)) register_10 (
    .D(DATA_IN), .en(demultiplexer_1_out9), .Q(register_10_q), .clk(Clock));  // open: clr
  Register_part #(.width(24)) register_11 (
    .D(DATA_IN), .en(demultiplexer_1_out10), .Q(register_11_q), .clk(Clock));  // open: clr
  Register_part #(.width(24)) register_12 (
    .D(DATA_IN), .en(demultiplexer_1_out11), .Q(register_12_q), .clk(Clock));  // open: clr
  Register_part #(.width(24)) register_13 (
    .D(DATA_IN), .en(demultiplexer_1_out12), .Q(register_13_q), .clk(Clock));  // open: clr
  Register_part #(.width(24)) register_14 (
    .D(DATA_IN), .en(demultiplexer_1_out13), .Q(register_14_q), .clk(Clock));  // open: clr
  Register_part #(.width(24)) register_15 (
    .D(DATA_IN), .en(demultiplexer_1_out14), .Q(register_15_q), .clk(Clock));  // open: clr
  Register_part #(.width(24)) register_16 (
    .D(DATA_IN), .en(demultiplexer_1_out15), .Q(register_16_q), .clk(Clock));  // open: clr
  Multiplexer #(.select(4), .width(24), .enable("false")) multiplexer_1 (
    .in0(register_1_q), .in1(register_2_q), .in2(register_3_q), .in3(register_4_q), .in4(register_5_q),
    .in5(register_6_q), .in6(register_7_q), .in7(register_8_q), .in8(register_9_q), .in9(register_10_q),
    .in10(register_11_q), .in11(register_12_q), .in12(register_13_q), .in13(register_14_q),
    .in14(register_15_q), .in15(register_16_q), .out(Data01), .sel(RS));
  Multiplexer #(.select(4), .width(24), .enable("false")) multiplexer_2 (
    .in0(register_1_q), .in1(register_2_q), .in2(register_3_q), .in3(register_4_q), .in4(register_5_q),
    .in5(register_6_q), .in6(register_7_q), .in7(register_8_q), .in8(register_9_q), .in9(register_10_q),
    .in10(register_11_q), .in11(register_12_q), .in12(register_13_q), .in13(register_14_q),
    .in14(register_15_q), .in15(register_16_q), .out(Data02), .sel(RT));
endmodule

module ALU_control (
  input  ALUOp0,
  input  ALUOp1,
  input  [3:0] Function,
  output [3:0] out_4
);

  wire ADD_out, NAND_out, NOR_out, OR_out, SLL_out, SLT_out, SRL_out, SUB_out, SW_LW_ADDI_out;

  and SW_LW_ADDI (SW_LW_ADDI_out, ~ALUOp1, ~ALUOp0);  // AND_Gate
  // AND_Gate AND has open pins: in0=ALUOp1, in1=Function[3], in2=Function[2], in3=Function[1], in4=Function[0], out=open
  and ADD (ADD_out, ALUOp1, ~Function[3], ~Function[2], Function[1], ~Function[0]);  // AND_Gate
  and OR (OR_out, ALUOp1, ~Function[3], ~Function[2], ~Function[1], Function[0]);  // AND_Gate
  and SLT (SLT_out, ALUOp1, ~Function[3], ~Function[2], Function[1], Function[0]);  // AND_Gate
  and NOR (NOR_out, ALUOp1, ~Function[3], Function[2], ~Function[1], ~Function[0]);  // AND_Gate
  and NAND (NAND_out, ALUOp1, ~Function[3], Function[2], ~Function[1], Function[0]);  // AND_Gate
  and SUB (SUB_out, ALUOp1, ~Function[3], Function[2], Function[1], ~Function[0]);  // AND_Gate
  and SRL (SRL_out, ALUOp1, ~Function[3], Function[2], Function[1], Function[0]);  // AND_Gate
  and SLL (SLL_out, ALUOp1, Function[3], ~Function[2], ~Function[1], ~Function[0]);  // AND_Gate
  or or_2 (out_4[0], NAND_out, SLT_out, OR_out, SRL_out);
  or or_3 (out_4[3], SUB_out, ALUOp0);
  or or_4 (out_4[1], SLT_out, ADD_out, SUB_out, SRL_out, SW_LW_ADDI_out, ALUOp0, SLL_out);
  or or_5 (out_4[2], NOR_out, NAND_out, SRL_out, SLL_out);

  // Notes on the sheet:
  //   Branch/SUBI
endmodule

module Control_Unit (
  input  [3:0] Input,
  output RegDest,
  output ALUSrc,
  output MemtoReg,
  output RegWrite,
  output MemRead,
  output MemWrite,
  output BEQ,
  output BNE,
  output Jump,
  output ALUOp1,
  output ALUOp0
);

  wire ADDI_out, SUBI_out;

  and R_type (ALUOp1, ~Input[3], ~Input[2], ~Input[1], ~Input[0]);  // AND_Gate
  and LW (MemRead, ~Input[3], Input[2], Input[1], Input[0]);  // AND_Gate
  and SW (MemWrite, Input[3], ~Input[2], ~Input[1], ~Input[0]);  // AND_Gate
  and u_BEQ (BEQ, Input[3], ~Input[2], ~Input[1], Input[0]);  // AND_Gate
  and u_BNE (BNE, Input[3], ~Input[2], Input[1], ~Input[0]);  // AND_Gate
  and u_JUMP (Jump, Input[3], Input[2], Input[1], Input[0]);
  and ADDI (ADDI_out, Input[3], ~Input[2], Input[1], Input[0]);  // AND_Gate
  and SUBI (SUBI_out, Input[3], Input[2], ~Input[1], ~Input[0]);  // AND_Gate
  or or_1 (ALUSrc, MemWrite, MemRead, ADDI_out, SUBI_out);
  or or_2 (RegWrite, MemRead, ALUOp1, ADDI_out, SUBI_out);
  or or_3 (ALUOp0, BEQ, SUBI_out, BNE);

  assign MemtoReg = MemRead;
  assign RegDest = ALUOp1;
endmodule

module ALU (
  input  [23:0] A,
  input  [23:0] B,
  input  [2:0] Operation,
  input  Carry_IN,
  input  Bit_inverter,
  input  [3:0] Shift,
  output [23:0] Output,
  output Zero_Flag,
  output Carry_OUT
);

  wire comparator_1_lt;
  wire [4:0] bit_extender_1_out;
  wire [23:0] adder_1_out, and_1_out, bit_extender_2_out, multiplexer_1_out, nand_1_out, nor_1_out,
       not_1_out, or_1_out, shifter_1_out, shifter_2_out;

  assign bit_extender_1_out = {{1{1'b0}}, Shift};  // Bit_Extender bit_extender_1
  assign not_1_out = ~B;  // NOT_Gate not_1, 24 bits wide
  Multiplexer #(.width(24), .enable("false")) multiplexer_1 (
    .in0(B), .in1(not_1_out), .out(multiplexer_1_out), .sel(Bit_inverter));
  Comparator #(.width(24)) comparator_1 (.a(A), .b(B), .lt(comparator_1_lt));  // open: gt, eq
  assign and_1_out = A & B;  // AND_Gate and_1, 24 bits wide
  assign or_1_out = A | B;  // OR_Gate or_1, 24 bits wide
  Adder #(.width(24)) adder_1 (.a(A), .b(multiplexer_1_out), .out(adder_1_out), .cin(Carry_IN), .cout(Carry_OUT));
  assign bit_extender_2_out = {{23{1'b0}}, comparator_1_lt};  // Bit_Extender bit_extender_2
  assign nor_1_out = ~(A | B);  // NOR_Gate nor_1, 24 bits wide
  assign nand_1_out = ~(A & B);  // NAND_Gate nand_1, 24 bits wide
  Shifter #(.width(24)) shifter_1 (.in(A), .\dist (bit_extender_1_out), .out(shifter_1_out));
  Shifter #(.width(24), .shift("lr")) shifter_2 (.in(A), .\dist (bit_extender_1_out), .out(shifter_2_out));
  Multiplexer #(.select(3), .width(24), .enable("false")) multiplexer_2 (
    .in0(and_1_out), .in1(or_1_out), .in2(adder_1_out), .in3(bit_extender_2_out), .in4(nor_1_out),
    .in5(nand_1_out), .in6(shifter_1_out), .in7(shifter_2_out), .out(Output), .sel(Operation));
  nor nor_2 (Zero_Flag, Output[0], Output[1], Output[2], Output[3], Output[4], Output[5], Output[6], Output[7], Output[8], Output[9], Output[10], Output[11], Output[12], Output[13], Output[14], Output[15], Output[16], Output[17], Output[18], Output[19], Output[20], Output[21], Output[22], Output[23]);
endmodule
